// Logisim project cpu.circ as structural Verilog: 15 circuits, main circuit main
module main (
  input  debug,
  input  beqz_t,
  input  [15:0] NPC_t,
  input  blt_t,
  input  reset,
  input  j_t,
  input  DMwe_t,
  input  Rwe_t,
  input  Rdst_t,
  input  Rwd_t,
  input  RwPC_t,
  input  KBr_t,
  input  TTYw_t,
  input  jr_t,
  input  ALUinImmed_t,
  input  [2:0] ALUop_t
);

  wire alu_1_z, ALUinImmed, and_1_out, and_2_out, beqz, blt, clk, DMwe, j, jr, KBr, keyboard_1_avail,
       memory_latch_1_oe_latched, memory_latch_1_we_latched, msb_1_msb, multiplexer_2_out, multiplexer_9_out,
       multiplexer_12_out, multiplexer_15_out, multiplexer_18_out, nclk, Rdst, Rwd, Rwe, RwPC, TTYw;
  wire [2:0] ALUop, multiplexer_3_out, multiplexer_5_out, rd, rs, rt, shamt;
  wire [3:0] opcode;
  wire [5:0] immed;
  wire [6:0] keyboard_1_data;
  wire [7:0] KBd;
  wire [11:0] address;
  wire [15:0] address_extender_1_extended, alu_1_opout, memory_latch_1_address_latched,
       memory_latch_1_data_in_latched, multiplexer_4_out, multiplexer_6_out, multiplexer_7_out,
       multiplexer_8_out, multiplexer_10_out, multiplexer_11_out, multiplexer_13_out, multiplexer_14_out,
       multiplexer_16_out, my_adder_1_result, nextpc_1_pc, NPC, ram_1_dout, RealNextPC,
       registerfile_1_reg2contents, rom_1_data, Rread, sign_extender_1_extended;

  Clock clock_1 (.out(clk));
  not not_1 (nclk, clk);
  Keyboard keyboard_1 (.clk(nclk), .re(KBr), .clr(reset), .avail(keyboard_1_avail), .data(keyboard_1_data));
  not not_2 (KBd[7], keyboard_1_avail);
  NextPC nextpc_1 (.Reset(reset), .RegIn(RealNextPC), .clk(nclk), .NextPC(NPC), .PC(nextpc_1_pc));
  ROM #(.addrWidth(16), .dataWidth(16)) rom_1 (.addr(nextpc_1_pc), .data(rom_1_data));
  Multiplexer #(.width(7), .enable("false")) multiplexer_1 (
    .in0(keyboard_1_data), .in1({7{1'b0}}), .out(KBd[6:0]), .sel(KBd[7]));
  TTY #(.rows(13), .cols(80)) tty_1 (.data(Rread[6:0]), .clk(clk), .we(TTYw), .clr(reset));
  Multiplexer #(.enable("false")) multiplexer_2 (.in0(Rdst), .in1(Rdst_t), .out(multiplexer_2_out), .sel(debug));
  InsnDecoder insndecoder_1 (
    .decodee(rom_1_data), .address(address), .opcode(opcode), .rs(rs), .rt(rt), .rd(rd), .shamt(shamt),
    .immed(immed));
  Multiplexer #(.width(3), .enable("false")) multiplexer_3 (
    .in0(rd), .in1(rt), .out(multiplexer_3_out), .sel(multiplexer_2_out));
  Multiplexer #(.width(16), .enable("false")) multiplexer_4 (
    .in0(multiplexer_16_out), .in1(NPC), .out(multiplexer_4_out), .sel(RwPC));
  Multiplexer #(.width(3), .enable("false")) multiplexer_5 (
    .in0(multiplexer_3_out), .in1(3'b111), .out(multiplexer_5_out), .sel(RwPC));
  RegisterFile registerfile_1 (
    .clk(clk), .reset(reset), .WriteData(multiplexer_4_out), .RegWriteEnable(Rwe),
    .WritePort(multiplexer_5_out), .ReadReg1(rs), .ReadReg2(rt), .Reg1Contents(Rread),
    .Reg2Contents(registerfile_1_reg2contents));
  Controller controller_1 (
    .opcode(opcode), .beqz(beqz), .blt(blt), .j(j), .DMwe(DMwe), .Rwe(Rwe), .Rdst(Rdst), .Rwd(Rwd),
    .RwPC(RwPC), .KBr(KBr), .TTYw(TTYw), .jr(jr), .ALUinImmed(ALUinImmed), .ALUop(ALUop));
  // Probe on sign_extender_1_extended
  sign_extender sign_extender_1 (.extend_in(immed), .extended(sign_extender_1_extended));
  Multiplexer #(.width(16), .enable("false")) multiplexer_6 (
    .in0(NPC), .in1(NPC_t), .out(multiplexer_6_out), .sel(debug));
  Multiplexer #(.width(16), .enable("false")) multiplexer_7 (
    .in0(Rread), .in1({{8{1'b0}}, KBd}), .out(multiplexer_7_out), .sel(KBr));
  Multiplexer #(.width(16), .enable("false")) multiplexer_8 (
    .in0(registerfile_1_reg2contents), .in1(sign_extender_1_extended), .out(multiplexer_8_out),
    .sel(ALUinImmed));
  my_adder my_adder_1 (
    .B(sign_extender_1_extended), .A(multiplexer_6_out), .sub(1'b0), .result(my_adder_1_result));  // open: ovf
  Multiplexer #(.enable("false")) multiplexer_9 (.in0(beqz), .in1(beqz_t), .out(multiplexer_9_out), .sel(debug));
  ALU alu_1 (
    .A(multiplexer_7_out), .B(multiplexer_8_out), .OpType(ALUop), .shamt(shamt), .Z(alu_1_z),
    .OpOut(alu_1_opout));
  and and_1 (and_1_out, multiplexer_9_out, alu_1_z);
  Multiplexer #(.width(16), .enable("false")) multiplexer_10 (
    .in0(NPC), .in1(NPC_t), .out(multiplexer_10_out), .sel(debug));
  Multiplexer #(.width(16), .enable("false")) multiplexer_11 (
    .in0(multiplexer_10_out), .in1(my_adder_1_result), .out(multiplexer_11_out), .sel(and_1_out));
  Multiplexer #(.enable("false")) multiplexer_12 (.in0(blt), .in1(blt_t), .out(multiplexer_12_out), .sel(debug));
  msb msb_1 (.all_bits(alu_1_opout), .msb(msb_1_msb));
  RAM #(.addrWidth(16), .dataWidth(16), .trigger("high"), .databus("bibus")) ram_1 (
    .addr(memory_latch_1_address_latched), .we(memory_latch_1_we_latched), .oe(memory_latch_1_oe_latched),
    .din(memory_latch_1_data_in_latched), .dout(ram_1_dout));
  memory_latch memory_latch_1 (
    .address(alu_1_opout), .WE(DMwe), .clk(nclk), .data_in(registerfile_1_reg2contents),
    .address_latched(memory_latch_1_address_latched), .WE_latched(memory_latch_1_we_latched),
    .OE_latched(memory_latch_1_oe_latched), .data_in_latched(memory_latch_1_data_in_latched));
  and and_2 (and_2_out, multiplexer_12_out, msb_1_msb);
  address_extender address_extender_1 (.extend_in(address), .extended(address_extender_1_extended));
  Multiplexer #(.width(16), .enable("false")) multiplexer_13 (
    .in0(multiplexer_11_out), .in1(my_adder_1_result), .out(multiplexer_13_out), .sel(and_2_out));
  Multiplexer #(.width(16), .enable("false")) multiplexer_14 (
    .in0(multiplexer_13_out), .in1(address_extender_1_extended), .out(multiplexer_14_out),
    .sel(multiplexer_15_out));
  Multiplexer #(.enable("false")) multiplexer_15 (.in0(j), .in1(j_t), .out(multiplexer_15_out), .sel(debug));
  Multiplexer #(.width(16), .enable("false")) multiplexer_16 (
    .in0(alu_1_opout), .in1(ram_1_dout), .out(multiplexer_16_out), .sel(Rwd));
  Multiplexer #(.width(16), .enable("false")) multiplexer_17 (
    .in0(multiplexer_14_out), .in1(Rread), .out(RealNextPC), .sel(multiplexer_18_out));
  Multiplexer #(.enable("false")) multiplexer_18 (.in0(jr), .in1(jr_t), .out(multiplexer_18_out), .sel(debug));

  // Other names for the same wires on the sheet: notav = KBd[7]

  // Notes on the sheet:
  //   contents of rom_1 (hex, n*v repeats v):
  //   2040 520d 2240 520d 2240 5209 2240 7380 2044 d013 2040 520d 2240 520d 2240 5209 2241 8340 903f 2dbd
  //   8cc0 8d01 8dc2 2082 a288 58 227f d013 160 267e d013 b28 b022 2141 7cc0 7d01 7dc2 2d83 ce00 ce00 219b
  //   903f 219c 903f
  //   Reg1 (rs) output
endmodule

module Controller (
  input  [3:0] opcode,
  output beqz,
  output blt,
  output j,
  output DMwe,
  output Rwe,
  output Rdst,
  output Rwd,
  output RwPC,
  output KBr,
  output TTYw,
  output jr,
  output ALUinImmed,
  output [2:0] ALUop
);

  wire decoder_1_out0, decoder_1_out1, decoder_1_out2, decoder_1_out3, decoder_1_out4, decoder_1_out5,
       decoder_1_out6, decoder_1_out11;

  Decoder #(.select(4)) decoder_1 (
    .out0(decoder_1_out0), .out1(decoder_1_out1), .out2(decoder_1_out2), .out3(decoder_1_out3),
    .out4(decoder_1_out4), .out5(decoder_1_out5), .out6(decoder_1_out6), .out7(Rwd), .out8(DMwe),
    .out9(beqz), .out10(blt), .out11(decoder_1_out11), .out12(jr), .out13(RwPC), .out14(KBr), .out15(TTYw),
    .sel(opcode));  // open: en
  or or_1 (ALUinImmed, decoder_1_out2, Rwd, DMwe);
  or or_2 (j, decoder_1_out11, RwPC);
  or or_3 (Rwe, decoder_1_out0, decoder_1_out1, decoder_1_out2, decoder_1_out3, decoder_1_out4, decoder_1_out5, decoder_1_out6, Rwd, RwPC, KBr);
  or or_4 (Rdst, decoder_1_out2, Rwd, RwPC);
  or or_5 (ALUop[2], decoder_1_out4, decoder_1_out5, decoder_1_out6);
  or or_6 (ALUop[1], decoder_1_out2, decoder_1_out3, decoder_1_out6, Rwd, DMwe);
  or or_7 (ALUop[0], decoder_1_out1, decoder_1_out3, decoder_1_out5, blt);
endmodule

module address_extender (
  input  [11:0] extend_in,
  output [15:0] extended
);


  assign extended = {4'b0000, extend_in};
endmodule

module msb (
  input  [15:0] all_bits,
  output msb
);


  assign msb = all_bits[15];
endmodule

module memory_latch (
  input  [15:0] address,
  input  WE,
  input  clk,
  input  [15:0] data_in,
  output [15:0] address_latched,
  output WE_latched,
  output OE_latched,
  output [15:0] data_in_latched
);

  wire DMwe_latch_q;
  wire [15:0] register_1_q;

  Register #(.width(16), .trigger("falling")) register_1 (
    .D(address), .en(WE), .clk(clk), .Q(register_1_q));  // open: clr
  D_Flip_Flop #(.trigger("falling")) DMwe_latch (.D(WE), .clk(clk), .Q(DMwe_latch_q));  // open: Qn, preset, reset
  Register #(.width(16), .trigger("falling")) data_to_be_written (
    .D(data_in), .en(WE), .clk(clk), .Q(data_in_latched));  // open: clr
  Multiplexer #(.width(16), .enable("false")) multiplexer_1 (
    .in0(address), .in1(register_1_q), .out(address_latched), .sel(DMwe_latch_q));
  and and_1 (WE_latched, clk, DMwe_latch_q);
  not not_1 (OE_latched, WE_latched);
endmodule

module sign_extender (
  input  [5:0] extend_in,
  output [15:0] extended
);


  assign extended = {{11{extend_in[5]}}, extend_in[4:0]};
endmodule

module InsnDecoder (
  input  [15:0] decodee,
  output [11:0] address,
  output [3:0] opcode,
  output [2:0] rs,
  output [2:0] rt,
  output [2:0] rd,
  output [2:0] shamt,
  output [5:0] immed
);


  assign address = decodee[11:0];
  assign immed = decodee[5:0];
  assign opcode = decodee[15:12];
  assign rd = decodee[5:3];
  assign rs = decodee[11:9];
  assign rt = decodee[8:6];
  assign shamt = decodee[2:0];
endmodule

module NextPC (
  input  Reset,
  input  [15:0] RegIn,
  input  clk,
  output [15:0] NextPC,
  output [15:0] PC
);

  my_register my_register_1 (.Reset(Reset), .Regin(RegIn), .WriteEnable(1'b1), .clk(clk), .RegOut(PC));
  my_adder my_adder_1 (.B(16'h1), .A(PC), .sub(1'b0), .result(NextPC));  // open: ovf
endmodule

module RegisterFile (
  input  clk,
  input  reset,
  input  [15:0] WriteData,
  input  RegWriteEnable,
  input  [2:0] WritePort,
  input  [2:0] ReadReg1,
  input  [2:0] ReadReg2,
  output [15:0] Reg1Contents,
  output [15:0] Reg2Contents
);

  wire out1bit0, out1bit1, out1bit2, out1bit3, out1bit4, out1bit5, out1bit6, out1bit7, out2bit0, out2bit1,
       out2bit2, out2bit3, out2bit4, out2bit5, out2bit6, out2bit7, WE1, WE2, WE3, WE4, WE5, WE6, WE7;
  wire [15:0] my_register_1_regout, my_register_2_regout, my_register_3_regout, my_register_4_regout,
       my_register_5_regout, my_register_6_regout, my_register_7_regout;

  Decoder #(.select(3)) decoder_1 (
    .out1(WE1), .out2(WE2), .out3(WE3), .out4(WE4), .out5(WE5), .out6(WE6), .out7(WE7), .sel(WritePort),
    .en(RegWriteEnable));  // open: out0
  Decoder #(.select(3)) decoder_2 (
    .out0(out1bit0), .out1(out1bit1), .out2(out1bit2), .out3(out1bit3), .out4(out1bit4), .out5(out1bit5),
    .out6(out1bit6), .out7(out1bit7), .sel(ReadReg1));  // open: en
  Decoder #(.select(3)) decoder_3 (
    .out0(out2bit0), .out1(out2bit1), .out2(out2bit2), .out3(out2bit3), .out4(out2bit4), .out5(out2bit5),
    .out6(out2bit6), .out7(out2bit7), .sel(ReadReg2));  // open: en
  my_register my_register_1 (
    .Reset(reset), .Regin(WriteData), .WriteEnable(WE1), .clk(clk), .RegOut(my_register_1_regout));
  my_register my_register_2 (
    .Reset(reset), .Regin(WriteData), .WriteEnable(WE2), .clk(clk), .RegOut(my_register_2_regout));
  my_register my_register_3 (
    .Reset(reset), .Regin(WriteData), .WriteEnable(WE3), .clk(clk), .RegOut(my_register_3_regout));
  my_register my_register_4 (
    .Reset(reset), .Regin(WriteData), .WriteEnable(WE4), .clk(clk), .RegOut(my_register_4_regout));
  my_register my_register_5 (
    .Reset(reset), .Regin(WriteData), .WriteEnable(WE5), .clk(clk), .RegOut(my_register_5_regout));
  my_register my_register_6 (
    .Reset(reset), .Regin(WriteData), .WriteEnable(WE6), .clk(clk), .RegOut(my_register_6_regout));
  my_register my_register_7 (
    .Reset(reset), .Regin(WriteData), .WriteEnable(WE7), .clk(clk), .RegOut(my_register_7_regout));
  assign Reg1Contents = out1bit0 ? {16{1'b0}} : 16'bz;  // Controlled_Buffer controlled_buffer_1
  assign Reg2Contents = out2bit0 ? {16{1'b0}} : 16'bz;  // Controlled_Buffer controlled_buffer_2
  assign Reg1Contents = out1bit1 ? my_register_1_regout : 16'bz;  // Controlled_Buffer controlled_buffer_3
  assign Reg2Contents = out2bit1 ? my_register_1_regout : 16'bz;  // Controlled_Buffer controlled_buffer_4
  assign Reg1Contents = out1bit2 ? my_register_2_regout : 16'bz;  // Controlled_Buffer controlled_buffer_5
  assign Reg2Contents = out2bit2 ? my_register_2_regout : 16'bz;  // Controlled_Buffer controlled_buffer_6
  assign Reg1Contents = out1bit3 ? my_register_3_regout : 16'bz;  // Controlled_Buffer controlled_buffer_7
  assign Reg2Contents = out2bit3 ? my_register_3_regout : 16'bz;  // Controlled_Buffer controlled_buffer_8
  assign Reg1Contents = out1bit4 ? my_register_4_regout : 16'bz;  // Controlled_Buffer controlled_buffer_9
  assign Reg2Contents = out2bit4 ? my_register_4_regout : 16'bz;  // Controlled_Buffer controlled_buffer_10
  assign Reg1Contents = out1bit5 ? my_register_5_regout : 16'bz;  // Controlled_Buffer controlled_buffer_11
  assign Reg2Contents = out2bit5 ? my_register_5_regout : 16'bz;  // Controlled_Buffer controlled_buffer_12
  assign Reg1Contents = out1bit6 ? my_register_6_regout : 16'bz;  // Controlled_Buffer controlled_buffer_13
  assign Reg2Contents = out2bit6 ? my_register_6_regout : 16'bz;  // Controlled_Buffer controlled_buffer_14
  assign Reg1Contents = out1bit7 ? my_register_7_regout : 16'bz;  // Controlled_Buffer controlled_buffer_15
  assign Reg2Contents = out2bit7 ? my_register_7_regout : 16'bz;  // Controlled_Buffer controlled_buffer_16
  // Probe on {16{1'b0}}
  // Probe on my_register_1_regout
  // Probe on my_register_2_regout
  // Probe on my_register_3_regout
  // Probe on my_register_4_regout
  // Probe on my_register_5_regout
  // Probe on my_register_6_regout
  // Probe on my_register_7_regout
endmodule

module my_register (
  input  Reset,
  input  [15:0] Regin,
  input  WriteEnable,
  input  clk,
  output [15:0] RegOut
);

  wire weclk;

  D_Flip_Flop d_ff_1 (.D(Regin[0]), .clk(weclk), .Q(RegOut[0]), .reset(Reset));  // open: Qn, preset
  D_Flip_Flop d_ff_2 (.D(Regin[4]), .clk(weclk), .Q(RegOut[4]), .reset(Reset));  // open: Qn, preset
  D_Flip_Flop d_ff_3 (.D(Regin[8]), .clk(weclk), .Q(RegOut[8]), .reset(Reset));  // open: Qn, preset
  D_Flip_Flop d_ff_4 (.D(Regin[12]), .clk(weclk), .Q(RegOut[12]), .reset(Reset));  // open: Qn, preset
  and and_1 (weclk, WriteEnable, clk);
  D_Flip_Flop d_ff_5 (.D(Regin[1]), .clk(weclk), .Q(RegOut[1]), .reset(Reset));  // open: Qn, preset
  D_Flip_Flop d_ff_6 (.D(Regin[5]), .clk(weclk), .Q(RegOut[5]), .reset(Reset));  // open: Qn, preset
  D_Flip_Flop d_ff_7 (.D(Regin[9]), .clk(weclk), .Q(RegOut[9]), .reset(Reset));  // open: Qn, preset
  D_Flip_Flop d_ff_8 (.D(Regin[13]), .clk(weclk), .Q(RegOut[13]), .reset(Reset));  // open: Qn, preset
  D_Flip_Flop d_ff_9 (.D(Regin[2]), .clk(weclk), .Q(RegOut[2]), .reset(Reset));  // open: Qn, preset
  D_Flip_Flop d_ff_10 (.D(Regin[6]), .clk(weclk), .Q(RegOut[6]), .reset(Reset));  // open: Qn, preset
  D_Flip_Flop d_ff_11 (.D(Regin[10]), .clk(weclk), .Q(RegOut[10]), .reset(Reset));  // open: Qn, preset
  D_Flip_Flop d_ff_12 (.D(Regin[14]), .clk(weclk), .Q(RegOut[14]), .reset(Reset));  // open: Qn, preset
  D_Flip_Flop d_ff_13 (.D(Regin[3]), .clk(weclk), .Q(RegOut[3]), .reset(Reset));  // open: Qn, preset
  D_Flip_Flop d_ff_14 (.D(Regin[7]), .clk(weclk), .Q(RegOut[7]), .reset(Reset));  // open: Qn, preset
  D_Flip_Flop d_ff_15 (.D(Regin[11]), .clk(weclk), .Q(RegOut[11]), .reset(Reset));  // open: Qn, preset
  D_Flip_Flop d_ff_16 (.D(Regin[15]), .clk(weclk), .Q(RegOut[15]), .reset(Reset));  // open: Qn, preset

  // Other names for the same wires on the sheet: in0 = Regin[0]; in1 = Regin[1]; in2 = Regin[2]; in3 = Regin[3];
  //   in4 = Regin[4]; in5 = Regin[5]; in6 = Regin[6]; in7 = Regin[7]; in8 = Regin[8]; in9 = Regin[9];
  //   in10 = Regin[10]; in11 = Regin[11]; in12 = Regin[12]; in13 = Regin[13]; in14 = Regin[14]; in15 = Regin[15];
  //   out0 = RegOut[0]; out1 = RegOut[1]; out2 = RegOut[2]; out3 = RegOut[3]; out4 = RegOut[4]; out5 = RegOut[5];
  //   out6 = RegOut[6]; out7 = RegOut[7]; out8 = RegOut[8]; out9 = RegOut[9]; out10 = RegOut[10]; out11 = RegOut[11];
  //   out12 = RegOut[12]; out13 = RegOut[13]; out14 = RegOut[14]; out15 = RegOut[15]; we = WriteEnable
endmodule

module ALU (
  input  [15:0] A,
  input  [15:0] B,
  input  [2:0] OpType,
  input  [2:0] shamt,
  output Z,
  output [15:0] OpOut
);

  wire or_1_out;
  wire [15:0] add, not0, sll0, srl0, sub, xor0;

  assign not0 = ~A;  // NOT_Gate not_1, 16 bits wide
  assign xor0 = A ^ B;  // XOR_Gate xor_1, 16 bits wide
  my_adder my_adder_1 (.B(B), .A(A), .sub(1'b0), .result(add));  // open: ovf
  my_adder my_adder_2 (.B(B), .A(A), .sub(1'b1), .result(sub));  // open: ovf
  left_shifter left_shifter_1 (.shift_in(A), .shift_3bit(shamt), .shift_out(sll0));
  right_shifter right_shifter_1 (.shift_in(A), .shift_3bit(shamt), .shift_out(srl0));
  or or_1 (or_1_out, A[0], A[1], A[2], A[3], A[4], A[5], A[6], A[7], A[8], A[9], A[10], A[11], A[12], A[13], A[14], A[15]);
  not not_2 (Z, or_1_out);
  Multiplexer #(.select(3), .width(16), .enable("false")) multiplexer_1 (
    .in0(add), .in1(sub), .in2(add), .in3(not0), .in4(xor0), .in5(sll0), .in6(srl0), .out(OpOut), .sel(OpType));  // open: in7
endmodule

module left_shifter (
  input  [15:0] shift_in,
  input  [2:0] shift_3bit,
  output [15:0] shift_out
);

  wire multiplexer_1_out, multiplexer_2_out, multiplexer_3_out, multiplexer_4_out, multiplexer_5_out,
       multiplexer_6_out, multiplexer_7_out, multiplexer_8_out, multiplexer_9_out, multiplexer_10_out,
       multiplexer_11_out, multiplexer_12_out, multiplexer_13_out, multiplexer_14_out, multiplexer_15_out,
       multiplexer_16_out, multiplexer_17_out, multiplexer_18_out, multiplexer_19_out, multiplexer_20_out,
       multiplexer_21_out, multiplexer_22_out, multiplexer_23_out, multiplexer_24_out, multiplexer_25_out,
       multiplexer_26_out, multiplexer_27_out, multiplexer_28_out, multiplexer_29_out, multiplexer_30_out,
       multiplexer_31_out, multiplexer_32_out;

  Multiplexer #(.enable("false")) multiplexer_1 (
    .in0(shift_in[0]), .in1(1'b0), .out(multiplexer_1_out), .sel(shift_3bit[2]));
  Multiplexer #(.enable("false")) multiplexer_2 (
    .in0(shift_in[1]), .in1(1'b0), .out(multiplexer_2_out), .sel(shift_3bit[2]));
  Multiplexer #(.enable("false")) multiplexer_3 (
    .in0(shift_in[2]), .in1(1'b0), .out(multiplexer_3_out), .sel(shift_3bit[2]));
  Multiplexer #(.enable("false")) multiplexer_4 (
    .in0(shift_in[3]), .in1(1'b0), .out(multiplexer_4_out), .sel(shift_3bit[2]));
  Multiplexer #(.enable("false")) multiplexer_5 (
    .in0(shift_in[4]), .in1(shift_in[0]), .out(multiplexer_5_out), .sel(shift_3bit[2]));
  Multiplexer #(.enable("false")) multiplexer_6 (
    .in0(shift_in[5]), .in1(shift_in[1]), .out(multiplexer_6_out), .sel(shift_3bit[2]));
  Multiplexer #(.enable("false")) multiplexer_7 (
    .in0(shift_in[6]), .in1(shift_in[2]), .out(multiplexer_7_out), .sel(shift_3bit[2]));
  Multiplexer #(.enable("false")) multiplexer_8 (
    .in0(shift_in[7]), .in1(shift_in[3]), .out(multiplexer_8_out), .sel(shift_3bit[2]));
  Multiplexer #(.enable("false")) multiplexer_9 (
    .in0(shift_in[8]), .in1(shift_in[4]), .out(multiplexer_9_out), .sel(shift_3bit[2]));
  Multiplexer #(.enable("false")) multiplexer_10 (
    .in0(shift_in[9]), .in1(shift_in[5]), .out(multiplexer_10_out), .sel(shift_3bit[2]));
  Multiplexer #(.enable("false")) multiplexer_11 (
    .in0(shift_in[10]), .in1(shift_in[6]), .out(multiplexer_11_out), .sel(shift_3bit[2]));
  Multiplexer #(.enable("false")) multiplexer_12 (
    .in0(shift_in[11]), .in1(shift_in[7]), .out(multiplexer_12_out), .sel(shift_3bit[2]));
  Multiplexer #(.enable("false")) multiplexer_13 (
    .in0(shift_in[12]), .in1(shift_in[8]), .out(multiplexer_13_out), .sel(shift_3bit[2]));
  Multiplexer #(.enable("false")) multiplexer_14 (
    .in0(shift_in[13]), .in1(shift_in[9]), .out(multiplexer_14_out), .sel(shift_3bit[2]));
  Multiplexer #(.enable("false")) multiplexer_15 (
    .in0(shift_in[14]), .in1(shift_in[10]), .out(multiplexer_15_out), .sel(shift_3bit[2]));
  Multiplexer #(.enable("false")) multiplexer_16 (
    .in0(shift_in[15]), .in1(shift_in[11]), .out(multiplexer_16_out), .sel(shift_3bit[2]));
  Multiplexer #(.enable("false")) multiplexer_17 (
    .in0(multiplexer_1_out), .in1(1'b0), .out(multiplexer_17_out), .sel(shift_3bit[1]));
  Multiplexer #(.enable("false")) multiplexer_18 (
    .in0(multiplexer_2_out), .in1(1'b0), .out(multiplexer_18_out), .sel(shift_3bit[1]));
  Multiplexer #(.enable("false")) multiplexer_19 (
    .in0(multiplexer_3_out), .in1(multiplexer_1_out), .out(multiplexer_19_out), .sel(shift_3bit[1]));
  Multiplexer #(.enable("false")) multiplexer_20 (
    .in0(multiplexer_4_out), .in1(multiplexer_2_out), .out(multiplexer_20_out), .sel(shift_3bit[1]));
  Multiplexer #(.enable("false")) multiplexer_21 (
    .in0(multiplexer_5_out), .in1(multiplexer_3_out), .out(multiplexer_21_out), .sel(shift_3bit[1]));
  Multiplexer #(.enable("false")) multiplexer_22 (
    .in0(multiplexer_6_out), .in1(multiplexer_4_out), .out(multiplexer_22_out), .sel(shift_3bit[1]));
  Multiplexer #(.enable("false")) multiplexer_23 (
    .in0(multiplexer_7_out), .in1(multiplexer_5_out), .out(multiplexer_23_out), .sel(shift_3bit[1]));
  Multiplexer #(.enable("false")) multiplexer_24 (
    .in0(multiplexer_8_out), .in1(multiplexer_6_out), .out(multiplexer_24_out), .sel(shift_3bit[1]));
  Multiplexer #(.enable("false")) multiplexer_25 (
    .in0(multiplexer_9_out), .in1(multiplexer_7_out), .out(multiplexer_25_out), .sel(shift_3bit[1]));
  Multiplexer #(.enable("false")) multiplexer_26 (
    .in0(multiplexer_10_out), .in1(multiplexer_8_out), .out(multiplexer_26_out), .sel(shift_3bit[1]));
  Multiplexer #(.enable("false")) multiplexer_27 (
    .in0(multiplexer_11_out), .in1(multiplexer_9_out), .out(multiplexer_27_out), .sel(shift_3bit[1]));
  Multiplexer #(.enable("false")) multiplexer_28 (
    .in0(multiplexer_12_out), .in1(multiplexer_10_out), .out(multiplexer_28_out), .sel(shift_3bit[1]));
  Multiplexer #(.enable("false")) multiplexer_29 (
    .in0(multiplexer_13_out), .in1(multiplexer_11_out), .out(multiplexer_29_out), .sel(shift_3bit[1]));
  Multiplexer #(.enable("false")) multiplexer_30 (
    .in0(multiplexer_14_out), .in1(multiplexer_12_out), .out(multiplexer_30_out), .sel(shift_3bit[1]));
  Multiplexer #(.enable("false")) multiplexer_31 (
    .in0(multiplexer_15_out), .in1(multiplexer_13_out), .out(multiplexer_31_out), .sel(shift_3bit[1]));
  Multiplexer #(.enable("false")) multiplexer_32 (
    .in0(multiplexer_16_out), .in1(multiplexer_14_out), .out(multiplexer_32_out), .sel(shift_3bit[1]));
  Multiplexer #(.enable("false")) multiplexer_33 (
    .in0(multiplexer_17_out), .in1(1'b0), .out(shift_out[0]), .sel(shift_3bit[0]));
  Multiplexer #(.enable("false")) multiplexer_34 (
    .in0(multiplexer_18_out), .in1(multiplexer_17_out), .out(shift_out[1]), .sel(shift_3bit[0]));
  Multiplexer #(.enable("false")) multiplexer_35 (
    .in0(multiplexer_19_out), .in1(multiplexer_18_out), .out(shift_out[2]), .sel(shift_3bit[0]));
  Multiplexer #(.enable("false")) multiplexer_36 (
    .in0(multiplexer_20_out), .in1(multiplexer_19_out), .out(shift_out[3]), .sel(shift_3bit[0]));
  Multiplexer #(.enable("false")) multiplexer_37 (
    .in0(multiplexer_21_out), .in1(multiplexer_20_out), .out(shift_out[4]), .sel(shift_3bit[0]));
  Multiplexer #(.enable("false")) multiplexer_38 (
    .in0(multiplexer_22_out), .in1(multiplexer_21_out), .out(shift_out[5]), .sel(shift_3bit[0]));
  Multiplexer #(.enable("false")) multiplexer_39 (
    .in0(multiplexer_23_out), .in1(multiplexer_22_out), .out(shift_out[6]), .sel(shift_3bit[0]));
  Multiplexer #(.enable("false")) multiplexer_40 (
    .in0(multiplexer_24_out), .in1(multiplexer_23_out), .out(shift_out[7]), .sel(shift_3bit[0]));
  Multiplexer #(.enable("false")) multiplexer_41 (
    .in0(multiplexer_25_out), .in1(multiplexer_24_out), .out(shift_out[8]), .sel(shift_3bit[0]));
  Multiplexer #(.enable("false")) multiplexer_42 (
    .in0(multiplexer_26_out), .in1(multiplexer_25_out), .out(shift_out[9]), .sel(shift_3bit[0]));
  Multiplexer #(.enable("false")) multiplexer_43 (
    .in0(multiplexer_27_out), .in1(multiplexer_26_out), .out(shift_out[10]), .sel(shift_3bit[0]));
  Multiplexer #(.enable("false")) multiplexer_44 (
    .in0(multiplexer_28_out), .in1(multiplexer_27_out), .out(shift_out[11]), .sel(shift_3bit[0]));
  Multiplexer #(.enable("false")) multiplexer_45 (
    .in0(multiplexer_29_out), .in1(multiplexer_28_out), .out(shift_out[12]), .sel(shift_3bit[0]));
  Multiplexer #(.enable("false")) multiplexer_46 (
    .in0(multiplexer_30_out), .in1(multiplexer_29_out), .out(shift_out[13]), .sel(shift_3bit[0]));
  Multiplexer #(.enable("false")) multiplexer_47 (
    .in0(multiplexer_31_out), .in1(multiplexer_30_out), .out(shift_out[14]), .sel(shift_3bit[0]));
  Multiplexer #(.enable("false")) multiplexer_48 (
    .in0(multiplexer_32_out), .in1(multiplexer_31_out), .out(shift_out[15]), .sel(shift_3bit[0]));

  // Other names for the same wires on the sheet: s_in0 = shift_3bit[0]; s_in1 = shift_3bit[1]; s_in2 = shift_3bit[2];
  //   in0 = shift_in[0]; in1 = shift_in[1]; in2 = shift_in[2]; in3 = shift_in[3]; in4 = shift_in[4];
  //   in5 = shift_in[5]; in6 = shift_in[6]; in7 = shift_in[7]; in8 = shift_in[8]; in9 = shift_in[9];
  //   in10 = shift_in[10]; in11 = shift_in[11]; in12 = shift_in[12]; in13 = shift_in[13]; in14 = shift_in[14];
  //   in15 = shift_in[15]; out0 = shift_out[0]; out1 = shift_out[1]; out2 = shift_out[2]; out3 = shift_out[3];
  //   out4 = shift_out[4]; out5 = shift_out[5]; out6 = shift_out[6]; out7 = shift_out[7]; out8 = shift_out[8];
  //   out9 = shift_out[9]; out10 = shift_out[10]; out11 = shift_out[11]; out12 = shift_out[12]; out13 = shift_out[13];
  //   out14 = shift_out[14]; out15 = shift_out[15]
endmodule

module right_shifter (
  input  [15:0] shift_in,
  input  [2:0] shift_3bit,
  output [15:0] shift_out
);

  wire multiplexer_1_out, multiplexer_2_out, multiplexer_3_out, multiplexer_4_out, multiplexer_5_out,
       multiplexer_6_out, multiplexer_7_out, multiplexer_8_out, multiplexer_9_out, multiplexer_10_out,
       multiplexer_11_out, multiplexer_12_out, multiplexer_13_out, multiplexer_14_out, multiplexer_15_out,
       multiplexer_16_out, multiplexer_17_out, multiplexer_18_out, multiplexer_19_out, multiplexer_20_out,
       multiplexer_21_out, multiplexer_22_out, multiplexer_23_out, multiplexer_24_out, multiplexer_25_out,
       multiplexer_26_out, multiplexer_27_out, multiplexer_28_out, multiplexer_29_out, multiplexer_30_out,
       multiplexer_31_out, multiplexer_32_out;

  Multiplexer #(.enable("false")) multiplexer_1 (
    .in0(shift_in[15]), .in1(1'b0), .out(multiplexer_1_out), .sel(shift_3bit[2]));
  Multiplexer #(.enable("false")) multiplexer_2 (
    .in0(shift_in[14]), .in1(1'b0), .out(multiplexer_2_out), .sel(shift_3bit[2]));
  Multiplexer #(.enable("false")) multiplexer_3 (
    .in0(shift_in[13]), .in1(1'b0), .out(multiplexer_3_out), .sel(shift_3bit[2]));
  Multiplexer #(.enable("false")) multiplexer_4 (
    .in0(shift_in[12]), .in1(1'b0), .out(multiplexer_4_out), .sel(shift_3bit[2]));
  Multiplexer #(.enable("false")) multiplexer_5 (
    .in0(shift_in[11]), .in1(shift_in[15]), .out(multiplexer_5_out), .sel(shift_3bit[2]));
  Multiplexer #(.enable("false")) multiplexer_6 (
    .in0(shift_in[10]), .in1(shift_in[14]), .out(multiplexer_6_out), .sel(shift_3bit[2]));
  Multiplexer #(.enable("false")) multiplexer_7 (
    .in0(shift_in[9]), .in1(shift_in[13]), .out(multiplexer_7_out), .sel(shift_3bit[2]));
  Multiplexer #(.enable("false")) multiplexer_8 (
    .in0(shift_in[8]), .in1(shift_in[12]), .out(multiplexer_8_out), .sel(shift_3bit[2]));
  Multiplexer #(.enable("false")) multiplexer_9 (
    .in0(shift_in[7]), .in1(shift_in[11]), .out(multiplexer_9_out), .sel(shift_3bit[2]));
  Multiplexer #(.enable("false")) multiplexer_10 (
    .in0(shift_in[6]), .in1(shift_in[10]), .out(multiplexer_10_out), .sel(shift_3bit[2]));
  Multiplexer #(.enable("false")) multiplexer_11 (
    .in0(shift_in[5]), .in1(shift_in[9]), .out(multiplexer_11_out), .sel(shift_3bit[2]));
  Multiplexer #(.enable("false")) multiplexer_12 (
    .in0(shift_in[4]), .in1(shift_in[8]), .out(multiplexer_12_out), .sel(shift_3bit[2]));
  Multiplexer #(.enable("false")) multiplexer_13 (
    .in0(shift_in[3]), .in1(shift_in[7]), .out(multiplexer_13_out), .sel(shift_3bit[2]));
  Multiplexer #(.enable("false")) multiplexer_14 (
    .in0(shift_in[2]), .in1(shift_in[6]), .out(multiplexer_14_out), .sel(shift_3bit[2]));
  Multiplexer #(.enable("false")) multiplexer_15 (
    .in0(shift_in[1]), .in1(shift_in[5]), .out(multiplexer_15_out), .sel(shift_3bit[2]));
  Multiplexer #(.enable("false")) multiplexer_16 (
    .in0(shift_in[0]), .in1(shift_in[4]), .out(multiplexer_16_out), .sel(shift_3bit[2]));
  Multiplexer #(.enable("false")) multiplexer_17 (
    .in0(multiplexer_1_out), .in1(1'b0), .out(multiplexer_17_out), .sel(shift_3bit[1]));
  Multiplexer #(.enable("false")) multiplexer_18 (
    .in0(multiplexer_2_out), .in1(1'b0), .out(multiplexer_18_out), .sel(shift_3bit[1]));
  Multiplexer #(.enable("false")) multiplexer_19 (
    .in0(multiplexer_3_out), .in1(multiplexer_1_out), .out(multiplexer_19_out), .sel(shift_3bit[1]));
  Multiplexer #(.enable("false")) multiplexer_20 (
    .in0(multiplexer_4_out), .in1(multiplexer_2_out), .out(multiplexer_20_out), .sel(shift_3bit[1]));
  Multiplexer #(.enable("false")) multiplexer_21 (
    .in0(multiplexer_5_out), .in1(multiplexer_3_out), .out(multiplexer_21_out), .sel(shift_3bit[1]));
  Multiplexer #(.enable("false")) multiplexer_22 (
    .in0(multiplexer_6_out), .in1(multiplexer_4_out), .out(multiplexer_22_out), .sel(shift_3bit[1]));
  Multiplexer #(.enable("false")) multiplexer_23 (
    .in0(multiplexer_7_out), .in1(multiplexer_5_out), .out(multiplexer_23_out), .sel(shift_3bit[1]));
  Multiplexer #(.enable("false")) multiplexer_24 (
    .in0(multiplexer_8_out), .in1(multiplexer_6_out), .out(multiplexer_24_out), .sel(shift_3bit[1]));
  Multiplexer #(.enable("false")) multiplexer_25 (
    .in0(multiplexer_9_out), .in1(multiplexer_7_out), .out(multiplexer_25_out), .sel(shift_3bit[1]));
  Multiplexer #(.enable("false")) multiplexer_26 (
    .in0(multiplexer_10_out), .in1(multiplexer_8_out), .out(multiplexer_26_out), .sel(shift_3bit[1]));
  Multiplexer #(.enable("false")) multiplexer_27 (
    .in0(multiplexer_11_out), .in1(multiplexer_9_out), .out(multiplexer_27_out), .sel(shift_3bit[1]));
  Multiplexer #(.enable("false")) multiplexer_28 (
    .in0(multiplexer_12_out), .in1(multiplexer_10_out), .out(multiplexer_28_out), .sel(shift_3bit[1]));
  Multiplexer #(.enable("false")) multiplexer_29 (
    .in0(multiplexer_13_out), .in1(multiplexer_11_out), .out(multiplexer_29_out), .sel(shift_3bit[1]));
  Multiplexer #(.enable("false")) multiplexer_30 (
    .in0(multiplexer_14_out), .in1(multiplexer_12_out), .out(multiplexer_30_out), .sel(shift_3bit[1]));
  Multiplexer #(.enable("false")) multiplexer_31 (
    .in0(multiplexer_15_out), .in1(multiplexer_13_out), .out(multiplexer_31_out), .sel(shift_3bit[1]));
  Multiplexer #(.enable("false")) multiplexer_32 (
    .in0(multiplexer_16_out), .in1(multiplexer_14_out), .out(multiplexer_32_out), .sel(shift_3bit[1]));
  Multiplexer #(.enable("false")) multiplexer_33 (
    .in0(multiplexer_17_out), .in1(1'b0), .out(shift_out[15]), .sel(shift_3bit[0]));
  Multiplexer #(.enable("false")) multiplexer_34 (
    .in0(multiplexer_18_out), .in1(multiplexer_17_out), .out(shift_out[14]), .sel(shift_3bit[0]));
  Multiplexer #(.enable("false")) multiplexer_35 (
    .in0(multiplexer_19_out), .in1(multiplexer_18_out), .out(shift_out[13]), .sel(shift_3bit[0]));
  Multiplexer #(.enable("false")) multiplexer_36 (
    .in0(multiplexer_20_out), .in1(multiplexer_19_out), .out(shift_out[12]), .sel(shift_3bit[0]));
  Multiplexer #(.enable("false")) multiplexer_37 (
    .in0(multiplexer_21_out), .in1(multiplexer_20_out), .out(shift_out[11]), .sel(shift_3bit[0]));
  Multiplexer #(.enable("false")) multiplexer_38 (
    .in0(multiplexer_22_out), .in1(multiplexer_21_out), .out(shift_out[10]), .sel(shift_3bit[0]));
  Multiplexer #(.enable("false")) multiplexer_39 (
    .in0(multiplexer_23_out), .in1(multiplexer_22_out), .out(shift_out[9]), .sel(shift_3bit[0]));
  Multiplexer #(.enable("false")) multiplexer_40 (
    .in0(multiplexer_24_out), .in1(multiplexer_23_out), .out(shift_out[8]), .sel(shift_3bit[0]));
  Multiplexer #(.enable("false")) multiplexer_41 (
    .in0(multiplexer_25_out), .in1(multiplexer_24_out), .out(shift_out[7]), .sel(shift_3bit[0]));
  Multiplexer #(.enable("false")) multiplexer_42 (
    .in0(multiplexer_26_out), .in1(multiplexer_25_out), .out(shift_out[6]), .sel(shift_3bit[0]));
  Multiplexer #(.enable("false")) multiplexer_43 (
    .in0(multiplexer_27_out), .in1(multiplexer_26_out), .out(shift_out[5]), .sel(shift_3bit[0]));
  Multiplexer #(.enable("false")) multiplexer_44 (
    .in0(multiplexer_28_out), .in1(multiplexer_27_out), .out(shift_out[4]), .sel(shift_3bit[0]));
  Multiplexer #(.enable("false")) multiplexer_45 (
    .in0(multiplexer_29_out), .in1(multiplexer_28_out), .out(shift_out[3]), .sel(shift_3bit[0]));
  Multiplexer #(.enable("false")) multiplexer_46 (
    .in0(multiplexer_30_out), .in1(multiplexer_29_out), .out(shift_out[2]), .sel(shift_3bit[0]));
  Multiplexer #(.enable("false")) multiplexer_47 (
    .in0(multiplexer_31_out), .in1(multiplexer_30_out), .out(shift_out[1]), .sel(shift_3bit[0]));
  Multiplexer #(.enable("false")) multiplexer_48 (
    .in0(multiplexer_32_out), .in1(multiplexer_31_out), .out(shift_out[0]), .sel(shift_3bit[0]));

  // Other names for the same wires on the sheet: s_in0 = shift_3bit[0]; s_in1 = shift_3bit[1]; s_in2 = shift_3bit[2];
  //   in0 = shift_in[0]; in1 = shift_in[1]; in2 = shift_in[2]; in3 = shift_in[3]; in4 = shift_in[4];
  //   in5 = shift_in[5]; in6 = shift_in[6]; in7 = shift_in[7]; in8 = shift_in[8]; in9 = shift_in[9];
  //   in10 = shift_in[10]; in11 = shift_in[11]; in12 = shift_in[12]; in13 = shift_in[13]; in14 = shift_in[14];
  //   in15 = shift_in[15]; out0 = shift_out[0]; out1 = shift_out[1]; out2 = shift_out[2]; out3 = shift_out[3];
  //   out4 = shift_out[4]; out5 = shift_out[5]; out6 = shift_out[6]; out7 = shift_out[7]; out8 = shift_out[8];
  //   out9 = shift_out[9]; out10 = shift_out[10]; out11 = shift_out[11]; out12 = shift_out[12]; out13 = shift_out[13];
  //   out14 = shift_out[14]; out15 = shift_out[15]
endmodule

module my_adder (
  input  [15:0] B,
  input  [15:0] A,
  input  sub,
  output [15:0] result,
  output ovf
);

  wire full_adder_1_cout, full_adder_2_cout, full_adder_3_cout, full_adder_4_cout, full_adder_5_cout,
       full_adder_6_cout, full_adder_7_cout, full_adder_8_cout, full_adder_9_cout, full_adder_10_cout,
       full_adder_11_cout, full_adder_12_cout, full_adder_13_cout, full_adder_14_cout, full_adder_15_cout,
       full_adder_16_cout, xor_1_out, xor_2_out, xor_3_out, xor_4_out, xor_5_out, xor_6_out, xor_7_out,
       xor_8_out, xor_9_out, xor_10_out, xor_11_out, xor_12_out, xor_13_out, xor_14_out, xor_15_out,
       xor_16_out;

  xor xor_1 (xor_1_out, sub, B[0]);
  xor xor_2 (xor_2_out, sub, B[1]);
  xor xor_3 (xor_3_out, sub, B[2]);
  xor xor_4 (xor_4_out, sub, B[3]);
  xor xor_5 (xor_5_out, sub, B[4]);
  xor xor_6 (xor_6_out, sub, B[5]);
  xor xor_7 (xor_7_out, sub, B[6]);
  xor xor_8 (xor_8_out, sub, B[7]);
  xor xor_9 (xor_9_out, sub, B[8]);
  xor xor_10 (xor_10_out, sub, B[9]);
  xor xor_11 (xor_11_out, sub, B[10]);
  xor xor_12 (xor_12_out, sub, B[11]);
  xor xor_13 (xor_13_out, sub, B[12]);
  xor xor_14 (xor_14_out, sub, B[13]);
  xor xor_15 (xor_15_out, sub, B[14]);
  xor xor_16 (xor_16_out, sub, B[15]);
  full_adder full_adder_1 (.Cin(sub), .A(A[0]), .B(xor_1_out), .result(result[0]), .Cout(full_adder_1_cout));
  full_adder full_adder_2 (
    .Cin(full_adder_1_cout), .A(A[1]), .B(xor_2_out), .result(result[1]), .Cout(full_adder_2_cout));
  full_adder full_adder_3 (
    .Cin(full_adder_2_cout), .A(A[2]), .B(xor_3_out), .result(result[2]), .Cout(full_adder_3_cout));
  full_adder full_adder_4 (
    .Cin(full_adder_3_cout), .A(A[3]), .B(xor_4_out), .result(result[3]), .Cout(full_adder_4_cout));
  full_adder full_adder_5 (
    .Cin(full_adder_4_cout), .A(A[4]), .B(xor_5_out), .result(result[4]), .Cout(full_adder_5_cout));
  full_adder full_adder_6 (
    .Cin(full_adder_5_cout), .A(A[5]), .B(xor_6_out), .result(result[5]), .Cout(full_adder_6_cout));
  full_adder full_adder_7 (
    .Cin(full_adder_6_cout), .A(A[6]), .B(xor_7_out), .result(result[6]), .Cout(full_adder_7_cout));
  full_adder full_adder_8 (
    .Cin(full_adder_7_cout), .A(A[7]), .B(xor_8_out), .result(result[7]), .Cout(full_adder_8_cout));
  full_adder full_adder_9 (
    .Cin(full_adder_8_cout), .A(A[8]), .B(xor_9_out), .result(result[8]), .Cout(full_adder_9_cout));
  full_adder full_adder_10 (
    .Cin(full_adder_9_cout), .A(A[9]), .B(xor_10_out), .result(result[9]), .Cout(full_adder_10_cout));
  full_adder full_adder_11 (
    .Cin(full_adder_10_cout), .A(A[10]), .B(xor_11_out), .result(result[10]), .Cout(full_adder_11_cout));
  full_adder full_adder_12 (
    .Cin(full_adder_11_cout), .A(A[11]), .B(xor_12_out), .result(result[11]), .Cout(full_adder_12_cout));
  full_adder full_adder_13 (
    .Cin(full_adder_12_cout), .A(A[12]), .B(xor_13_out), .result(result[12]), .Cout(full_adder_13_cout));
  full_adder full_adder_14 (
    .Cin(full_adder_13_cout), .A(A[13]), .B(xor_14_out), .result(result[13]), .Cout(full_adder_14_cout));
  full_adder full_adder_15 (
    .Cin(full_adder_14_cout), .A(A[14]), .B(xor_15_out), .result(result[14]), .Cout(full_adder_15_cout));
  full_adder full_adder_16 (
    .Cin(full_adder_15_cout), .A(A[15]), .B(xor_16_out), .result(result[15]), .Cout(full_adder_16_cout));
  xor xor_17 (ovf, full_adder_15_cout, full_adder_16_cout);

  // Notes on the sheet:
  //   LSB (0)
  //   MSB (15)
endmodule

module full_adder (
  input  Cin,
  input  A,
  input  B,
  output result,
  output Cout
);

  wire and_1_out, and_2_out, xor_1_out;

  and and_1 (and_1_out, B, A);
  xor xor_1 (xor_1_out, A, B);
  or or_1 (Cout, and_1_out, and_2_out);
  and and_2 (and_2_out, xor_1_out, Cin);
  xor xor_2 (result, Cin, xor_1_out);
endmodule
